# Fritzing sketch PingClearanceWiring (saved by Fritzing 0.9.3b)
breadboards: 1

parts:
  Part1 = Arduino Uno (Rev3)
  hc-sr1 = hc-sr04
  LED1 = LED - 3mm [color="Red (633nm)" package="3 mm [THT]"]
  LED2 = LED - 3mm [color="Red (633nm)" package="3 mm [THT]"]
  R1 = Resistor [tolerance=±5% resistance=220 package="0402 [SMD]"]
  R2 = Resistor [tolerance=±5% resistance=220 package="0402 [SMD]"]

nets:
  N1: Part1.D11_PWM/MOSI, hc-sr1.Echo
  N2: Part1.D12/MISO, hc-sr1.Trig
  N3: Part1.D2, R1.Pin_1
  N4: Part1.D3_PWM, R2.Pin_1
  5V: Part1.5V, hc-sr1.VCC
  GND: Part1.GND, hc-sr1.GND
  N5: LED1.cathode, LED2.cathode
  N6: LED1.anode, R1.Pin_0
  N7: LED2.anode, R2.Pin_0
